# Fritzing sketch perfboard-design (saved by Fritzing 0.9.3b)
perfboards: 1

parts:
  Teensy_3_1 = Teensy 3.1
  J1 = Screw terminal - 2 pins [package=THT]
  J2 = Screw terminal - 2 pins [package=THT]
  J3 = Screw terminal - 2 pins [package=THT]
  J4 = Screw terminal - 2 pins [package=THT]
  J5 = Screw terminal - 2 pins [package=THT]
  J6 = Screw terminal - 2 pins [package=THT]
  J7 = Screw terminal - 2 pins [package=THT]
  J8 = Screw terminal - 2 pins [package=THT]
  J9 = Screw terminal - 2 pins [package=THT]  # not connected
  J10 = Screw terminal - 2 pins [package=THT]  # not connected
  J11 = Screw terminal - 2 pins [package=THT]
  J12 = Screw terminal - 2 pins [package=THT]
  J13 = Screw terminal - 2 pins [package=THT]
  J14 = Screw terminal - 2 pins [package=THT]  # not connected
  IC1 = ULN2803A [package=THT]
  C1 = Electrolytic Capacitor [capacitance=0.47mF voltage=50V package="1010 [SMD, electrolytic]"]
  J15 = Screw terminal - 2 pins [package=THT]
  U1 = Vibration Motor- ROB-08449 [package=vibe-motor-10mm]
  U2 = Vibration Motor- ROB-08449 [package=vibe-motor-10mm]
  U3 = Vibration Motor- ROB-08449 [package=vibe-motor-10mm]
  U4 = Vibration Motor- ROB-08449 [package=vibe-motor-10mm]
  U5 = Vibration Motor- ROB-08449 [package=vibe-motor-10mm]
  U6 = Vibration Motor- ROB-08449 [package=vibe-motor-10mm]
  U7 = Vibration Motor- ROB-08449 [package=vibe-motor-10mm]
  U8 = Vibration Motor- ROB-08449 [package=vibe-motor-10mm]
  J16 = Screw terminal - 2 pins [package=THT]  # not connected
  LED1 = smd LED [color="Red (633nm)" package="0805 [SMD]"]
  J17 = Screw terminal - 2 pins [package=THT]  # not connected
  LED2 = smd LED [color="Red (633nm)" package="0805 [SMD]"]
  U9 = Header 1 [package=1x01_offset]
  U10 = Header 1 [package=1x01_offset]  # not connected
  LED3 = smd LED [color="Red (633nm)" package="0805 [SMD]"]
  LED4 = smd LED [color="Red (633nm)" package="0805 [SMD]"]
  LED5 = smd LED [color="Red (633nm)" package="0805 [SMD]"]
  LED6 = smd LED [color="Red (633nm)" package="0805 [SMD]"]
  LED7 = smd LED [color="Red (633nm)" package="0805 [SMD]"]
  LED8 = smd LED [color="Red (633nm)" package="0805 [SMD]"]
  R1 = Resistor [tolerance=±5% resistance=220 package="0402 [SMD]"]
  R2 = Resistor [tolerance=±5% resistance=220 package="0402 [SMD]"]
  R3 = Resistor [tolerance=±5% resistance=220 package="0402 [SMD]"]
  R4 = Resistor [tolerance=±5% resistance=220 package="0402 [SMD]"]
  R5 = Resistor [tolerance=±5% resistance=220 package="0402 [SMD]"]
  R6 = Resistor [tolerance=±5% resistance=220 package="0402 [SMD]"]
  R7 = Resistor [tolerance=±5% resistance=220 package="0402 [SMD]"]
  R8 = Resistor [tolerance=±5% resistance=220 package="0402 [SMD]"]
  S1 = Pushbutton [package="[THT]"]
  S2 = Pushbutton [package="[THT]"]
  S3 = Pushbutton [package="[THT]"]
  J18 = Screw terminal - 2 pins [package=THT]  # not connected
  C2 = Electrolytic Capacitor [capacitance=0.47mF voltage=50V package="1010 [SMD, electrolytic]"]

nets:
  N1: Teensy_3_1.D3, IC1.In_8
  N2: Teensy_3_1.D4, IC1.In_7
  N3: Teensy_3_1.D5, IC1.In_6
  N4: Teensy_3_1.D6, IC1.In_5
  N5: Teensy_3_1.D9, IC1.In_2
  N6: Teensy_3_1.D10, IC1.In_1
  N7: Teensy_3_1.D11, Teensy_3_1.3V3, S1.Pin_1, S1.Pin_2
  N8: Teensy_3_1.D12, S2.Pin_1, S2.Pin_2
  N9: Teensy_3_1.A0/D14, S3.Pin_1, S3.Pin_2
  N10: Teensy_3_1.A4/D18, J11.pin2
  N11: Teensy_3_1.A5/D19, J12.pin1
  N12: Teensy_3_1.A6/D20, IC1.In_3
  N13: Teensy_3_1.A7/D21, IC1.In_4
  N14: Teensy_3_1.A8/D22, J13.pin1
  N15: Teensy_3_1.A9/D23, J13.pin2
  N16: J1.pin1, J1.pin2, J8.pin2, U7.+, U8.+
  N17: J2.pin1, U1.-, U2.-
  N18: J2.pin2, J3.pin1, J3.pin2, U1.+, U2.+
  N19: J4.pin1, U3.-, U4.-
  N20: J4.pin2, J5.pin1, J5.pin2, U3.+, U4.+
  N21: J6.pin1, U5.-, U6.-
  N22: J6.pin2, J7.pin1, J7.pin2, U5.+, U6.+
  N23: J8.pin1, U7.-, U8.-
  N24: IC1.0V, C1.+, C2.-
  N25: IC1.COM_-_Common, C1.-, J15.pin2
  N26: LED1.anode, R4.Pin_0
  N27: LED2.anode, R5.Pin_0
  N28: U9.1, R8.Pin_1
  N29: LED3.anode, R3.Pin_0
  N30: LED4.anode, R2.Pin_0
  N31: LED5.anode, R1.Pin_0
  N32: LED6.anode, R6.Pin_0
  N33: LED7.anode, R7.Pin_0
  N34: LED8.anode, R8.Pin_0
  N35: S1.Pin_3, S1.Pin_4
  N36: S2.Pin_3, S2.Pin_4
  N37: S3.Pin_3, S3.Pin_4
